// Logisim project processor_riscv_evolutionbu.circ as structural Verilog
module ALU (
  input  [31:0] A,
  input  [31:0] B,
  input  [2:0] F,
  output Zero,
  output [31:0] Y
);

  wire bitselector_1_out;
  wire [31:0] adder_1_out, adder_2_out, and_1_out, bit_extender_1_out, not_1_out, or_1_out;

  assign not_1_out = ~B;  // NOT_Gate not_1, 32 bits wide
  Adder #(.width(32)) adder_1 (.a(A), .b(B), .out(adder_1_out), .cin(1'b0));  // open: cout
  Adder #(.width(32)) adder_2 (.a(A), .b(not_1_out), .out(adder_2_out), .cin(1'b1));  // open: cout
  assign and_1_out = A & B;  // AND_Gate and_1, 32 bits wide
  assign or_1_out = A | B;  // OR_Gate or_1, 32 bits wide
  assign bit_extender_1_out = {{31{bitselector_1_out}}, bitselector_1_out};  // Bit_Extender bit_extender_1
  BitSelector #(.width(32)) bitselector_1 (.in(adder_2_out), .out(bitselector_1_out), .sel({5{1'b1}}));
  Multiplexer #(.select(3), .width(32)) multiplexer_1 (
    .in0(adder_1_out), .in1(adder_2_out), .in2(and_1_out), .in3(or_1_out), .in5(bit_extender_1_out), .out(Y),
    .sel(F));  // open: in4, in6, in7
  nor nor_1 (Zero, Y[0], Y[1], Y[2], Y[3], Y[4], Y[5], Y[6], Y[7], Y[8], Y[9], Y[10], Y[11], Y[12], Y[13], Y[14], Y[15], Y[16], Y[17], Y[18], Y[19], Y[20], Y[21], Y[22], Y[23], Y[24], Y[25], Y[26], Y[27], Y[28], Y[29], Y[30], Y[31]);
endmodule

module Datapath (
  output [31:0] out_1,
  output [31:0] t2
);

  wire alu_1_zero, and_1_out, clock_1_out, controlunit_1_alusrc, controlunit_1_branch, controlunit_1_regwrite;
  wire [2:0] controlunit_1_alucontrol;
  wire [7:0] adder_1_out, adder_2_out, bit_extender_2_out, multiplexer_1_out, register_1_q, shifter_1_out;
  wire [11:0] multiplexer_2_out, shifter_2_out;
  wire [31:0] alu_1_y, bit_extender_1_out, multiplexer_3_out, registerfile_1_rd1, registerfile_1_rd2;

  Multiplexer #(.width(8)) multiplexer_1 (
    .in0(adder_1_out), .in1(adder_2_out), .out(multiplexer_1_out), .sel(and_1_out));
  Clock clock_1 (.out(clock_1_out));
  Register register_1 (.D(multiplexer_1_out), .en(1'b1), .clk(clock_1_out), .Q(register_1_q));  // open: clr
  Shifter #(.shift("lr")) shifter_1 (.in(register_1_q), .\dist (3'b010), .out(shifter_1_out));
  Adder adder_1 (.a(register_1_q), .b(8'h4), .out(adder_1_out));  // open: cin, cout
  ROM #(.dataWidth(32)) rom_1 (.addr(shifter_1_out), .data(out_1));
  Multiplexer #(.width(12)) multiplexer_2 (
    .in0(out_1[31:20]), .in1(shifter_2_out), .out(multiplexer_2_out), .sel(and_1_out));
  Shifter #(.width(12)) shifter_2 (
    .in({out_1[31], out_1[7], out_1[30:25], out_1[11:8]}), .\dist (4'b0001), .out(shifter_2_out));
  RegisterFile registerfile_1 (
    .WD3(alu_1_y), .CLK(clock_1_out), .A2(out_1[22:20]), .A1(out_1[17:15]), .A3(out_1[9:7]),
    .WE3(controlunit_1_regwrite), .RD1(registerfile_1_rd1), .RD2(registerfile_1_rd2), .T2(t2));
  assign bit_extender_1_out = {{20{multiplexer_2_out[11]}}, multiplexer_2_out};  // Bit_Extender bit_extender_1
  Bit_Extender #(.in_width(32), .out_width(8)) bit_extender_2 (.in(bit_extender_1_out), .out(bit_extender_2_out));
  ControlUnit controlunit_1 (
    .Instruction(out_1), .RegWrite(controlunit_1_regwrite), .ALUSrc(controlunit_1_alusrc),
    .Branch(controlunit_1_branch), .ALUControl(controlunit_1_alucontrol));
  Multiplexer #(.width(32)) multiplexer_3 (
    .in0(registerfile_1_rd2), .in1(bit_extender_1_out), .out(multiplexer_3_out), .sel(controlunit_1_alusrc));
  Adder adder_2 (.a(register_1_q), .b(bit_extender_2_out), .out(adder_2_out));  // open: cin, cout
  ALU alu_1 (
    .A(registerfile_1_rd1), .B(multiplexer_3_out), .F(controlunit_1_alucontrol), .Y(alu_1_y),
    .Zero(alu_1_zero));
  and and_1 (and_1_out, controlunit_1_branch, alu_1_zero);

  // Notes on the sheet:
  //   contents of rom_1 (hex, n*v repeats v):
  //   300293 100393 28333 2030263 38133 fff30313 30663 2383b3 fe000ae3 fff28313 302b3 fe0000e3 63 400293
  //   228393 5383b3 538663 ffd38393 fe000ce3 33
endmodule

module RegisterFile (
  input  CLK,
  input  [2:0] A1,
  input  [31:0] WD3,
  input  [2:0] A2,
  input  WE3,
  input  [2:0] A3,
  output [31:0] RD1,
  output [31:0] RD2,
  output [31:0] T2
);

  wire and_1_out, and_2_out, and_3_out, and_4_out, and_5_out, and_6_out, and_7_out, decoder_1_out0,
       decoder_1_out1, decoder_1_out2, decoder_1_out3, decoder_1_out4, decoder_1_out5, decoder_1_out6,
       decoder_1_out7;
  wire [31:0] register_1_q, register_2_q, register_3_q, register_4_q, register_5_q, register_6_q;

  Decoder #(.select(3)) decoder_1 (
    .out0(decoder_1_out0), .out1(decoder_1_out1), .out2(decoder_1_out2), .out3(decoder_1_out3),
    .out4(decoder_1_out4), .out5(decoder_1_out5), .out6(decoder_1_out6), .out7(decoder_1_out7), .sel(A3));  // open: en
  and and_1 (and_1_out, WE3, decoder_1_out1);
  and and_2 (and_2_out, WE3, decoder_1_out2);
  and and_3 (and_3_out, WE3, decoder_1_out3);
  and and_4 (and_4_out, WE3, decoder_1_out4);
  and and_5 (and_5_out, WE3, decoder_1_out5);
  and and_6 (and_6_out, WE3, decoder_1_out6);
  and and_7 (and_7_out, WE3, decoder_1_out7);
  Register #(.width(32)) register_1 (.D(WD3), .en(and_1_out), .clk(CLK), .Q(register_1_q));  // open: clr
  Register #(.width(32)) register_2 (.D(WD3), .en(and_2_out), .clk(CLK), .Q(register_2_q));  // open: clr
  Register #(.width(32)) register_3 (.D(WD3), .en(and_3_out), .clk(CLK), .Q(register_3_q));  // open: clr
  Register #(.width(32)) register_4 (.D(WD3), .en(and_4_out), .clk(CLK), .Q(register_4_q));  // open: clr
  Register #(.width(32)) register_5 (.D(WD3), .en(and_5_out), .clk(CLK), .Q(register_5_q));  // open: clr
  Register #(.width(32)) register_6 (.D(WD3), .en(and_6_out), .clk(CLK), .Q(register_6_q));  // open: clr
  Register #(.width(32)) register_7 (.D(WD3), .en(and_7_out), .clk(CLK), .Q(T2));  // open: clr
  Multiplexer #(.enable("true"), .select(3), .width(32)) multiplexer_1 (
    .in0({32{1'b0}}), .in1(register_1_q), .in2(register_2_q), .in3(register_3_q), .in4(register_4_q),
    .in5(register_5_q), .in6(register_6_q), .in7(T2), .out(RD1), .sel(A1));  // open: en
  Multiplexer #(.enable("true"), .select(3), .width(32)) multiplexer_2 (
    .in0({32{1'b0}}), .in1(register_1_q), .in2(register_2_q), .in3(register_3_q), .in4(register_4_q),
    .in5(register_5_q), .in6(register_6_q), .in7(T2), .out(RD2), .sel(A2));  // open: en
endmodule

module ControlUnit (
  input  [31:0] Instruction,
  output RegWrite,
  output ALUSrc,
  output [2:0] ALUControl,
  output Branch
);

  wire comparator_3_eq;
  wire [2:0] bit_extender_1_out;

  Comparator #(.mode("unsigned"), .width(7)) comparator_1 (
    .a(Instruction[6:0]), .b(7'b1100011), .eq(Branch));  // open: gt, lt
  Comparator #(.mode("unsigned"), .width(7)) comparator_2 (
    .a(Instruction[6:0]), .b(7'b0010011), .eq(ALUSrc));  // open: gt, lt
  Comparator #(.mode("unsigned"), .width(7)) comparator_3 (
    .a(Instruction[6:0]), .b(7'b0110011), .eq(comparator_3_eq));  // open: gt, lt
  not not_1 (RegWrite, Branch);
  or or_1 (RegWrite, ALUSrc, comparator_3_eq);
  assign bit_extender_1_out = {{2{Branch}}, Branch};  // Bit_Extender bit_extender_1
  assign ALUControl = 3'b001 & bit_extender_1_out;  // AND_Gate and_1, 3 bits wide

  // Notes on the sheet:
  //   beq
  //   addi
  //   r-t
endmodule

module Tests (
  output [31:0] Y,
  output [3:0] out_2,
  output [7:0] out_3
);


  assign out_2 = 4'b0010;
  assign out_3 = 8'h22;
  assign Y = 32'hf4010207;

  // Notes on the sheet:
  //   binary values in Logisim. Convince yourself how the bits are displayed.
  //   Example 1: A simple example that illustrates how 32-bit values are displayed as 
  //   Example 2) An example of how to extra certain bits from a (in this case) 32-bit wire. Here we extract the bits 8..11 from the 32-bit wire.
  //   Example 3) Sometimes it is useful to extra bits from different position and the re-assemble them. In this case, we extract bits 8..11 and bits 15..18 and assemble them into an 8-bit wire.
endmodule
